# Fritzing sketch ArduinoBlinky (saved by Fritzing 0.9.3b)
breadboards: 1

parts:
  Part1 = Arduino Uno (Rev3)
  R1 = Resistor [tolerance=±5% resistance=1k package="2512 [SMD]"]
  LED1 = smd LED [color="Red (633nm)" package="0805 [SMD]"]

nets:
  N1: Part1.D11_PWM/MOSI, R1.Pin_1
  N2: Part1.GND, LED1.cathode
  N3: R1.Pin_0, LED1.anode
