# Fritzing sketch Feather Servos (saved by Fritzing 0.9.3b)
breadboards: 1

parts:
  Part1 = Adafruit Feather HUZZAH ESP8266 [part_number="Adafruit #2821"]
  POT1 = Breadboard Trimpot
  R1 = Resistor [tolerance=±5% resistance=10k package=THT]
  R2 = Resistor [tolerance=±5% resistance=5.1k package="2010 [SMD]"]
  R3 = Resistor [tolerance=±5% resistance=3k package="2010 [SMD]"]
  R4 = Resistor [tolerance=±5% resistance=1k package="2010 [SMD]"]
  J1 = Basic Servo
  U1 = SWITCH_SPDT [package=kps-1290]

nets:
  N1: Part1.ADC, POT1.PIN2
  GND: Part1.GND, POT1.PIN3, R4.Pin_1, J1.gnd
  N2: Part1.3.3V, R1.Pin_0
  N3: Part1.VBUS, U1.P
  N4: Part1.GPIO2, J1.pulse
  N5: POT1.PIN1, R1.Pin_1, R2.Pin_0
  N6: R2.Pin_1, R3.Pin_0
  N7: R3.Pin_1, R4.Pin_0
  N8: J1.vcc, U1.S

notes:
  Voltage Splitter (3.3V -> 1V)
  3.3V ->
  10K - Output - 5.1K
  -> 3K -> 1K -> GND
  Inline Switch lets us turn off the Servo when we don't want it to run

custom parts:
  Adafruit Feather HUZZAH ESP8266: his is the Adafruit Feather HUZZAH ESP8266 - our take on an 'all-in-one' ESP8266 WiFi development board with built in USB and battery charging. Its an ESP8266 WiFi module with all the extras you need, ready to rock! We have other boards in the Feather family, check'em out here. At the Feather HUZZAH's heart is an ESP8266 WiFi microcontroller clocked at 80 MHz and at 3.3V logic. This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
